# Fritzing sketch pcb (saved by Fritzing 0.9.3b)
circuit board: 8cm x 12cm
breadboards: 1

parts:
  R1 = Resistor [tolerance=±5% resistance=100k package=THT]
  R2 = Resistor [tolerance=±5% resistance=100k package=THT]
  R3 = Resistor [tolerance=±5% resistance=100k package=THT]
  R4 = Resistor [tolerance=±5% resistance=100k package=THT]
  R5 = Resistor [tolerance=±5% resistance=100k package=THT]
  R7 = Resistor [tolerance=±5% resistance=100k package=THT]
  R8 = Resistor [tolerance=±5% resistance=100k package=THT]
  R9 = Resistor [tolerance=±5% resistance=100k package=THT]
  R10 = Resistor [tolerance=±5% resistance=100k package=THT]
  R6 = Resistor [tolerance=±5% resistance=100k package=THT]
  button_connector = screw terminal, 20 pins
  Pro_Micro = IC, DIP package, 24 pins [chip_label=IC]

nets:
  N1: R1.Pin_0, button_connector.pin1, Pro_Micro.pin2
  N2: R1.Pin_1, R2.Pin_1, R3.Pin_1, R4.Pin_1, R5.Pin_1, R7.Pin_1, R8.Pin_1, R9.Pin_1, R10.Pin_1, R6.Pin_1, Pro_Micro.pin11
  N3: R2.Pin_0, button_connector.pin3, Pro_Micro.pin1
  N4: R3.Pin_0, button_connector.pin5, Pro_Micro.pin24
  N5: R4.Pin_0, button_connector.pin7, Pro_Micro.pin23
  N6: R5.Pin_0, button_connector.pin9, Pro_Micro.pin22
  N7: R7.Pin_0, button_connector.pin13, Pro_Micro.pin20
  N8: R8.Pin_0, button_connector.pin15, Pro_Micro.pin19
  N9: R9.Pin_0, button_connector.pin17, Pro_Micro.pin18
  N10: R10.Pin_0, button_connector.pin19, Pro_Micro.pin17
  N11: R6.Pin_0, button_connector.pin11, Pro_Micro.pin21
  N12: button_connector.pin2, button_connector.pin4, button_connector.pin6, button_connector.pin8, button_connector.pin10, button_connector.pin12, button_connector.pin14, button_connector.pin16, button_connector.pin18, button_connector.pin20, Pro_Micro.pin9

notes:
  USB
  01
  assignments:
  02
  03
  04
  05
  06
  07
  08
  09
  10
